# Fritzing sketch NSR_CDI_V0.4 (saved by Fritzing 0.9.3b)
breadboards: 1

parts:
  U1 = NodeMCU V3.0
  U2 = Sharp PC817 [part_number=PC817XI package=SMT]
  R3 = Resistor [tolerance=±5% resistance=220 package=THT]
  R4 = Resistor [tolerance=±5% resistance=470 package=THT]
  SCR1 = SCR [part_number=5P4M package="TO220 [THT]"]
  C6 = Tantalum Capacitor [capacitance=0.1µF voltage=35V package="100 mil [THT, tantalum]"]
  C7 = Ceramic Capacitor [capacitance=3.3µF voltage=0.4kV package="200 mil [THT, multilayer]"]
  C8 = Ceramic Capacitor [capacitance=3.3µF voltage=0.4kV package="200 mil [THT, multilayer]"]
  D2 = Rectifier Diode [part_number=1N5408 package="300 mil [THT]"]
  D3 = Rectifier Diode [part_number=1N5408 package="300 mil [THT]"]
  C9 = Electrolytic Capacitor [capacitance=220µF voltage=50V package="200 mil [THT, electrolytic]"]
  R5 = Resistor [tolerance=±5% resistance=1.2k package=THT]
  R6 = Resistor [tolerance=±5% resistance=330 package=THT]
  Q1 = NPN-Transistor [package="TO92 [THT]"]
  R7 = Resistor [tolerance=±5% resistance=1.2k package=THT]
  IC1 = Voltage Regulator [package=78xxl]
  C10 = Electrolytic Capacitor [capacitance=220µF voltage=50V package="200 mil [THT, electrolytic]"]
  LED1 = smd LED [color="Red (633nm)" package="0603 [SMD]"]
  D4 = Rectifier Diode [part_number=1N4007 package="300 mil [THT]"]
  D5 = Rectifier Diode [part_number=1N4007 package="300 mil [THT]"]
  D6 = Rectifier Diode [part_number=1N4007 package="300 mil [THT]"]
  D7 = Rectifier Diode [part_number=1N4007 package="300 mil [THT]"]
  D8 = Rectifier Diode [part_number=1N4007 package="300 mil [THT]"]

nets:
  N1: U1.D1, U2.Pin_3, R4.Pin_1, C6.+
  N2: U1.D4, R6.Pin_1
  N3: U1.GND#6, U1.GND#13, U1.GND#16, U1.GND#33, U2.Pin_2, R4.Pin_0, SCR1.K, C6.-, D3.anode, C9.-, R7.Pin_1, IC1.GND, C10.-
  N4: U1.D6, R5.Pin_0
  N5: U1.Vin, U2.Pin_4, Q1.B, IC1.OUT, C10.+
  N6: U2.Pin_1, R3.Pin_1
  N7: R3.Pin_0, LED1.cathode
  N8: SCR1.A, C8.0, D2.cathode
  N9: SCR1.G, Q1.E, R7.Pin_0
  N10: C7.1, D2.anode, D3.cathode
  N11: C9.+, D5.anode
  N12: R5.Pin_1, Q1.C
  N13: IC1.IN, D8.cathode
  N14: D4.cathode, D7.anode
  N15: D4.anode, D5.cathode
  N16: D6.cathode, D8.anode
  N17: D6.anode, D7.cathode

notes:
  Nodemcu V2
  PC817
  470Ω
  330Ω
  LED
  接脈衝訊號 (青/黃)
  接激磁線圈 (紅/黑)
  電門熄火開關 (黑/白)可不接
  麥拉 3.3㎌/400V
  麥拉 1.5㎌/400V
  1N5408
  1N5408
  SCR BT151-500R
  接 RC (紅/白)
  接高壓線圈 (黃/黑)
  接地(綠)
  Zener 5.1V
  470㎌ / 35V
  7805
  VCC 接電門正電 12V
  此排 12V
  此排 5V
  NSR-150
  可程式化 CDI V0.4 版
  By 羽山 https://3wa.tw
  鉭質 0.1㎌ / 35V
  2SC1815
  1.2KΩ
  1.2KΩ
  220Ω
  1N4007 x 5

custom parts:
  NodeMCU V3.0: ESP8266 based NodeMCU
  SCR: Silicon Controlled Rectifier - TO220
